// Digital circuit ALU_Integração.dig as structural Verilog
module \ALU_Integração  (
  input  [2:0] OP,
  input  [7:0] N,
  input  CLK,
  input  EN,
  output [7:0] AC,
  output [7:0] MQ,
  output [7:0] AC_2
);

  wire somador_subtrator_8bits_1_cout, somador_subtrator_8bits_2_cout;
  wire [7:0] MULT_LSB, MULT_MSB, MUX_AC, MUX_MQ, notconnected_1_out, notconnected_2_out, notconnected_3_out,
       notconnected_4_out, notconnected_5_out, notconnected_6_out, R_ADD, R_DIV_q, R_NAND, R_SHL, R_SHR,
       R_SUB, R_XOR;

  somador_subtrator_8bits somador_subtrator_8bits_1 (
    .A(AC), .B(N), .SUB(1'b0), .COUT(somador_subtrator_8bits_1_cout), .S(R_ADD));
  somador_subtrator_8bits somador_subtrator_8bits_2 (
    .A(AC), .B(N), .SUB(1'b1), .COUT(somador_subtrator_8bits_2_cout), .S(R_SUB));
  // XOR xor_1: pin names not known; wires that end beside it: N, AC, R_XOR
  // NAND nand_1: pin names not known; wires that end beside it: N, AC, R_NAND
  Shift_Left shift_left_1 (.AC(AC), .S(R_SHL));
  Shift_Right shift_right_1 (.AC(AC), .S(R_SHR));
  Mul #(.Bits(8)) mul_1 (.a(N), .b(AC), .mul({MULT_MSB, MULT_LSB}));
  Div #(.Bits(8)) div_1 (.a(N), .b(AC), .q(R_DIV_q), .r(AC_2));
  LED OVERFLOW (.in(somador_subtrator_8bits_1_cout));
  LED OVERFLOW_2 (.in(somador_subtrator_8bits_2_cout));
  Multiplexer #(.Bits(8), .Selector_Bits(3)) multiplexer_1 (
    .sel(OP), .in_0(R_ADD), .in_1(R_SUB), .in_2(MULT_LSB), .in_3(AC_2), .in_4(R_SHL), .in_5(R_SHR),
    .in_6(R_NAND), .in_7(R_XOR), .out(MUX_AC));
  Multiplexer #(.Selector_Bits(3), .Bits(8)) multiplexer_2 (
    .sel(OP), .in_0(notconnected_1_out), .in_1(notconnected_2_out), .in_2(MULT_MSB), .in_3(R_DIV_q),
    .in_4(notconnected_3_out), .in_5(notconnected_4_out), .in_6(notconnected_5_out),
    .in_7(notconnected_6_out), .out(MUX_MQ));
  // NotConnected on notconnected_1_out
  // NotConnected on notconnected_2_out
  // NotConnected on notconnected_3_out
  // NotConnected on notconnected_4_out
  // NotConnected on notconnected_5_out
  // NotConnected on notconnected_6_out
  Register #(.Bits(8)) REG_AC (.D(MUX_AC), .C(CLK), .en(EN), .Q(AC));
  Register #(.Bits(8)) REG_MQ (.D(MUX_MQ), .C(CLK), .en(EN), .Q(MQ));

  // Other names for the same wires on the sheet: R_DIV_r[7:0] = AC_2

  // Notes on the sheet:
  //   OP0 - Adição
  //   OP1 - Subtração
  //   OP2 - Multiplicação
  //   OP3 - Divisão
  //   OP4 - Shift Left
  //   OP5 - Shift Right
  //   OP6 - NAND
  //   OP7 - XOR
  //   ALU - Integração
  //   Aqui estaremos integrando todos os módulos criados
endmodule
