// Digital circuit CPU - OLD - step counter + decoder (one-hot control).dig as structural Verilog
module CPU___OLD___step_counter___decoder__one_hot_control (
  input  EN,
  input  clr,
  input  CLOCK,
  output [7:0] out_4,
  output [7:0] out_5,
  output [7:0] out_6,
  output [7:0] out_7,
  output [3:0] out_8
);

  wire counter_1_ovf, MAR_EN, T0, T1, T2, T3, T4, T5, T6, T7;
  wire [2:0] Counter;
  wire [7:0] MAR_D;

  PC pc_1 (.CLOCK(T2), .PC_OUT(out_5));
  Counter #(.Bits(3)) counter_1 (.en(EN), .C(CLOCK), .clr(clr), .out(Counter), .ovf(counter_1_ovf));
  LED led_1 (.in(counter_1_ovf));
  assign MAR_D = out_5 | {4'b0000, out_4[3:0]};  // Or or_1, 8 bits wide
  or or_2 (MAR_EN, T1, T3);
  Decoder #(.Selector_Bits(3)) decoder_1 (
    .sel(Counter), .out_0(T0), .out_1(T1), .out_2(T2), .out_3(T3), .out_4(T4), .out_5(T5), .out_6(T6),
    .out_7(T7));
  Register #(.Bits(8)) register_1 (.D(MAR_D), .C(CLOCK), .en(MAR_EN), .Q(out_6));
  RAMDualPort #(.AddrBits(8), .isProgramMemory("true"), .Bits(8)) ramdualport_1 (
    .A(out_6), .Din({8{1'b0}}), .str(1'b0), .C(CLOCK), .ld(1'b1), .D(out_7));
  Register #(.Bits(8)) register_2 (.D(out_7), .C(CLOCK), .en(T2), .Q(out_4));

  assign out_8 = out_4[3:0];

  // Other names for the same wires on the sheet: MAR_OUT[7:0] = out_6; IR_ADDR[3:0] = out_4[3:0];
  //   OP[3:0] = out_4[7:4]; PC_OUT[7:0] = out_5; RAM_D[7:0] = out_7

  // Notes on the sheet:
  //   Ciclo de Fetch
  //   PC
  //   CPU - step counter + decoder (one-hot control)
  //   Aqui estaremos integrando todos os módulos criados 
  //   para a produção da CPU
  //   CONTADOR
  //   MAR
  //   RAM
  //   IR
endmodule
