// Digital circuit CPU - Ring counter + tri-state bus.dig as structural Verilog
module CPU___Ring_counter___tri_state_bus (
  input  EN,
  input  clr,
  input  L_M,
  input  L_I,
  input  clk,
  output [3:0] DEBUG_BUS_LOW,
  output [3:0] DEBUG_PC,
  output [3:0] DEBUG_BUS_LOW_2,
  output [3:0] DEBUG_BUS_HIGH,
  output [7:0] AC,
  output [7:0] MQ,
  output [7:0] DEBUG_Numero,
  output [3:0] DEBUG_OP_CODE,
  output [3:0] DEBUG_IR,
  output [2:0] DEBUG_OP_CODE2
);

  wire BUS, counter_1_ovf, IR, Q0, Q1, Q2, Q3;
  wire [3:0] register_1_q, register_2_q;

  ring_counter ring_counter_1 (.CLK(clk), .T1(Q0), .T2(Q1), .T3(Q2), .T4(Q3));
  or or_1 (IR, Q2, Q3);
  Counter #(.Bits(4)) counter_1 (.en(EN), .C(Q3), .clr(clr), .out(DEBUG_PC), .ovf(counter_1_ovf));
  LED led_1 (.in(counter_1_ovf));
  Register #(.Bits(4)) register_1 (.D(DEBUG_BUS_LOW), .C(clk), .en(~L_M), .Q(register_1_q));
  Register #(.Bits(4)) register_2 (.D(DEBUG_BUS_LOW), .C(clk), .en(~L_M), .Q(register_2_q));
  EEPROMDualPort #(.AddrBits(4), .Bits(8)) eepromdualport_1 (
    .A(DEBUG_BUS_LOW), .Din({8{1'b0}}), .str(1'b0), .C(clk), .ld(1'b1), .D(DEBUG_Numero));
  EEPROMDualPort #(.AddrBits(4), .Bits(4)) eepromdualport_2 (
    .A(DEBUG_BUS_HIGH), .Din(4'b0000), .str(1'b0), .C(clk), .ld(1'b1), .D(DEBUG_OP_CODE));
  Register #(.Bits(4)) register_3 (.D(DEBUG_OP_CODE), .C(clk), .en(~L_I), .Q(DEBUG_IR));
  assign DEBUG_BUS_LOW = Q3 ? DEBUG_PC : 4'bz;  // Driver driver_1
  assign DEBUG_BUS_LOW = Q0 ? register_1_q : 4'bz;  // Driver driver_2
  assign DEBUG_BUS_HIGH = Q1 ? register_2_q : 4'bz;  // Driver driver_3
  assign DEBUG_BUS_HIGH = IR ? DEBUG_IR : 4'bz;  // Driver driver_4
  // NotConnected on BUS
  assign DEBUG_OP_CODE2 = IR ? DEBUG_BUS_HIGH[2:0] : 3'bz;  // Driver driver_5
  \ALU_Integração  \alu_integração_1  (.OP(DEBUG_OP_CODE2), .N(DEBUG_Numero), .CLK(clk), .EN(Q3), .AC(AC), .MQ(MQ));

  assign DEBUG_BUS_LOW_2 = DEBUG_BUS_LOW;

  // Other names for the same wires on the sheet: BUS_HIGH[3:0] = DEBUG_BUS_HIGH; BUS_LOW[3:0] = DEBUG_BUS_LOW;
  //   nL_I = L_I; nL_M = L_M; Numero[7:0] = DEBUG_Numero; OP_CODE[3:0] = DEBUG_OP_CODE; T1 = Q0; T2 = Q1; T3 = Q2;
  //   T4 = Q3

  // Notes on the sheet:
  //   Ring Counter
  //   CC
  //   RING COUNTER
  //   CPU - Ring counter + tri-state bus
  //   Aqui estaremos integrando todos os módulos criados 
  //   para a produção da CPU
  //   OP0 - Adição
  //   OP1 - Subtração
  //   OP2 - Multiplicação
  //   OP3 - Divisão
  //   OP4 - Shift Left
  //   OP5 - Shift Right
  //   OP6 - NAND
  //   OP7 - XOR
  //   PC (Program Counter)
  //   MAR (Memory Acess Register)
  //   RAM 16x2 (RANDOM ACCESS MEMORY)
  //   IR (INSTRUCTION REGISTER)
  //   PC
  //   (Program Counter)
  //   (Memory Acess Register)
  //   MAR
  //   contents of eepromdualport_1 (hex, n*v repeats v):
  //   2,3,4,9,3
  //   contents of eepromdualport_2 (hex, n*v repeats v):
  //   a0,1,2,3,4,5,6,7
  //   ALU (Arithmetic Logic Unit)
endmodule
