// Digital circuit CPU_8Bits.dig as structural Verilog
module CPU_8Bits (
  input  EN,
  input  clr,
  input  CLOCK,
  output [7:0] out_4,
  output [7:0] out_5,
  output [7:0] out_6,
  output [7:0] out_7
);

  wire counter_1_ovf, T0, T1, T2, T3, T4, T5, T6, T7;
  wire [2:0] Counter;

  PC pc_1 (.CLOCK(T2), .PC_OUT(out_5));
  Counter #(.Bits(3)) counter_1 (.en(EN), .C(CLOCK), .clr(clr), .out(Counter), .ovf(counter_1_ovf));
  LED led_1 (.in(counter_1_ovf));
  Decoder #(.Selector_Bits(3)) decoder_1 (
    .sel(Counter), .out_0(T0), .out_1(T1), .out_2(T2), .out_3(T3), .out_4(T4), .out_5(T5), .out_6(T6),
    .out_7(T7));
  Register #(.Bits(8)) register_1 (.D(out_5), .C(CLOCK), .en(T1), .Q(out_6));
  RAMDualPort #(.AddrBits(8), .Bits(8)) ramdualport_1 (
    .A(out_6), .Din({8{1'b0}}), .str(1'b0), .C(CLOCK), .ld(1'b1), .D(out_7));
  Register #(.Bits(8)) register_2 (.D(out_7), .C(CLOCK), .en(T2), .Q(out_4));

  // Other names for the same wires on the sheet: MAR_OUT[7:0] = out_6; PC_OUT[7:0] = out_5; RAM_D[7:0] = out_7

  // Notes on the sheet:
  //   Ciclo de Fetch
  //   CONTADOR
  //   PC
  //   CPU - Integração
  //   Aqui estaremos integrando todos os módulos criados 
  //   para a produção da CPU
  //   MAR
  //   RAM
  //   IR
endmodule
