// Digital circuit D-FlipFlop.dig as structural Verilog
module D_FlipFlop (
  input  DATA,
  input  STORE,
  output S
);

  wire d_latch_1_s, not_1_out;

  not not_1 (not_1_out, STORE);
  D_Latch d_latch_1 (.DATA(DATA), .STORE(not_1_out), .S(d_latch_1_s));
  D_Latch d_latch_2 (.DATA(d_latch_1_s), .STORE(STORE), .S(S));

  // Notes on the sheet:
  //   D-FLIP-FLOP
  //   Diminui sensibilidade em relação ao D-Latch 
  //   e aumenta previlibilidade com clock
  //   O Flip Flop altera na borda do clock (store)
endmodule
