// Digital circuit D-Latch.dig as structural Verilog
module D_Latch (
  input  DATA,
  input  STORE,
  output S
);

  wire and_1_out, and_2_out, nor_1_out, not_1_out;

  not not_1 (not_1_out, DATA);
  and and_1 (and_1_out, DATA, STORE);
  and and_2 (and_2_out, STORE, not_1_out);
  nor nor_1 (nor_1_out, and_1_out, S);
  nor nor_2 (S, nor_1_out, and_2_out);

  // Notes on the sheet:
  //   D-Latch
  //   Armazenamento de estados simples (1 ou 0)
endmodule
