// Digital circuit PC.dig as structural Verilog
module PC (
  input  CLOCK,
  output [7:0] PC_OUT
);

  wire somador_subtrator_8bits_1_cout;
  wire [7:0] PC_plus_1;

  Register #(.Bits(8)) register_1 (.D(PC_plus_1), .C(CLOCK), .en(1'b1), .Q(PC_OUT));
  Seven_Seg_Hex seven_seg_hex_1 (.d(PC_OUT[3:0]), .dp(1'b0));
  somador_subtrator_8bits somador_subtrator_8bits_1 (
    .A(PC_OUT), .B(8'h1), .SUB(1'b0), .COUT(somador_subtrator_8bits_1_cout), .S(PC_plus_1));
  // also tied to GND on the sheet: {somador_subtrator_8bits_1_cout, PC_OUT[4], PC_OUT[5], PC_OUT[6], PC_OUT[7]}

  // Notes on the sheet:
  //   Entradas
  //   Registrador do PC
  //   PC - Program Counter
  //   O PC define o endereço da próxima instrução a ser executada
  //   Somador + 1
endmodule
