// Digital circuit PC_OLD.dig as structural Verilog
module PC_OLD (
  input  [7:0] DATA,
  input  LOAD,
  input  CLOCK,
  input  INC
);

  wire or_1_out;
  wire [7:0] PC, PC_OUT, PC_plus_1;

  or or_1 (or_1_out, LOAD, INC);
  REG_AC_8Bit reg_ac_8bit_1 (.DATA(PC), .STORE_AC(or_1_out), .CLOCK(CLOCK), .D(PC_OUT));
  Seven_Seg_Hex seven_seg_hex_1 (.d(PC_OUT[3:0]), .dp(1'b0));
  somador_subtrator_8bits somador_subtrator_8bits_1 (.A(PC_OUT), .B(8'h1), .SUB(1'b0), .S(PC_plus_1));  // open: COUT
  Multiplexer #(.Selector_Bits(2), .Bits(8)) multiplexer_1 (
    .sel({LOAD, INC}), .in_0(PC_OUT), .in_1(PC_plus_1), .in_2(DATA), .in_3(DATA), .out(PC));

  // Notes on the sheet:
  //   Entradas
  //   ENABLE
  //   PC - Program Counter
  //   O PC define o endereço da próxima instrução a ser executada
  //   Registrador do PC
  //   Somador + 1
  //   Seletor de operando
endmodule
