// Digital circuit REG_1Bit.dig as structural Verilog
module REG_1Bit (
  input  DATA,
  input  Store,
  input  CLOCK,
  output S
);

  wire and_1_out, and_2_out, not_1_out, or_1_out;

  not not_1 (not_1_out, Store);
  and and_1 (and_1_out, S, not_1_out);
  and and_2 (and_2_out, Store, DATA);
  or or_1 (or_1_out, and_1_out, and_2_out);
  D_FlipFlop d_flipflop_1 (.DATA(or_1_out), .STORE(CLOCK), .S(S));

  // Notes on the sheet:
  //   Registrador de 1bit
endmodule
