// Digital circuit REG_MQ_8Bit.dig as structural Verilog
module REG_MQ_8Bit (
  input  [7:0] DATA,
  input  STORE_MQ,
  input  CLOCK,
  output [7:0] D
);

  REG_1Bit reg_1bit_1 (.DATA(DATA[0]), .Store(STORE_MQ), .CLOCK(CLOCK), .S(D[0]));
  REG_1Bit reg_1bit_2 (.DATA(DATA[1]), .Store(STORE_MQ), .CLOCK(CLOCK), .S(D[1]));
  REG_1Bit reg_1bit_3 (.DATA(DATA[2]), .Store(STORE_MQ), .CLOCK(CLOCK), .S(D[2]));
  REG_1Bit reg_1bit_4 (.DATA(DATA[3]), .Store(STORE_MQ), .CLOCK(CLOCK), .S(D[3]));
  REG_1Bit reg_1bit_5 (.DATA(DATA[4]), .Store(STORE_MQ), .CLOCK(CLOCK), .S(D[4]));
  REG_1Bit reg_1bit_6 (.DATA(DATA[5]), .Store(STORE_MQ), .CLOCK(CLOCK), .S(D[5]));
  REG_1Bit reg_1bit_7 (.DATA(DATA[6]), .Store(STORE_MQ), .CLOCK(CLOCK), .S(D[6]));
  REG_1Bit reg_1bit_8 (.DATA(DATA[7]), .Store(STORE_MQ), .CLOCK(CLOCK), .S(D[7]));

  // Other names for the same wires on the sheet: D_0 = D[0]; D_1 = D[1]; D_2 = D[2]; D_3 = D[3]; D_4 = D[4];
  //   D_5 = D[5]; D_6 = D[6]; D_7 = D[7]; D0 = DATA[0]; D1 = DATA[1]; D2 = DATA[2]; D3 = DATA[3]; D4 = DATA[4];
  //   D5 = DATA[5]; D6 = DATA[6]; D7 = DATA[7]; STORE = STORE_MQ

  // Notes on the sheet:
  //   Multiplier Quotient Register (MQ) de 8bits
  //   Armazena estado de 8 bits de forma consistente, 
  //   com enable de load (store) e clock para sincronia
endmodule
