// Digital circuit Seletor.dig as structural Verilog
module Seletor (
  input  [7:0] R_ADD,
  input  [7:0] R_SUB,
  input  [7:0] R_XOR,
  input  [7:0] R_NAND,
  input  [7:0] R_SHL,
  input  [7:0] R_SHR,
  input  [7:0] R_MULT,
  input  [7:0] R_DIV,
  input  [2:0] OP,
  output [7:0] S
);

  Multiplexer #(.Bits(8), .Selector_Bits(3)) multiplexer_1 (
    .sel(OP), .in_0(R_ADD), .in_1(R_SUB), .in_2(R_XOR), .in_3(R_NAND), .in_4(R_SHL), .in_5(R_SHR),
    .in_6(R_MULT), .in_7(R_DIV), .out(S));

  // Notes on the sheet:
  //   Seletor
  //   Seleciona qual opração será armazenada no registrador
endmodule
