// Digital circuit Shift_Left.dig as structural Verilog
module Shift_Left (
  input  [7:0] AC,
  output [7:0] S
);


  assign S = {AC[6:0], 1'b0};

  // Notes on the sheet:
  //   Shift Left
  //   Desloca todos os bits para a esquerda (Multiplica por dois)
  //   Descarta o MSB
  //   Insere 0 no LSB
endmodule
