// Digital circuit Shift_Right.dig as structural Verilog
module Shift_Right (
  input  [7:0] AC,
  output [7:0] S
);


  assign S = {1'b0, AC[7:1]};

  // Notes on the sheet:
  //   Shift Right
  //   Desloca todos os bits para a direita (Divide por dois)
  //   Descarta o LSB
  //   Insere 0 no MSB
endmodule
