// Digital circuit Shift_Right_16bits.dig as structural Verilog
module Shift_Right_16bits (
  input  [15:0] AC,
  output [15:0] S
);

  // Pins of 8 and 16 bits meet at AC
  // Pins of 8 and 16 bits meet at {1'b0, AC[15:1]}

  assign S = {1'b0, AC[15:1]};

  // Notes on the sheet:
  //   Shift Right 16bits
  //   Desloca todos os bits para a direita (Divide por dois)
  //   Descarta o LSB
  //   Insere 0 no MSB
endmodule
