// Digital circuit XOR.dig as structural Verilog
module XOR (
  input  [7:0] AC,
  input  [7:0] N,
  output [7:0] S
);

  assign S = AC ^ N;  // XOr xor_1, 8 bits wide

  // Notes on the sheet:
  //   XOR
endmodule
