// Digital circuit multiplicador_8bits.dig as structural Verilog
module multiplicador_8bits (
  input  [7:0] A,
  input  STORE,
  input  CLOCK,
  input  [7:0] B,
  input  START,
  output [7:0] MSB,
  output [7:0] LSB
);

  wire [7:0] AC_NEXT, DATA_AC, DATA_MQ, Reg_AC, Reg_MQ, S;

  Multiplexer #(.Bits(8)) multiplexer_1 (.sel(START), .in_0(DATA_AC), .in_1({8{1'b0}}), .out(Reg_AC));
  Multiplexer #(.Bits(8)) multiplexer_2 (.sel(START), .in_0(DATA_MQ), .in_1(B), .out(Reg_MQ));
  somador_subtrator_8bits somador_subtrator_8bits_1 (.A(MSB), .B(A), .SUB(1'b0), .S(S));  // open: COUT
  REG_AC_8Bit reg_ac_8bit_1 (.DATA(Reg_AC), .STORE_AC(STORE), .CLOCK(CLOCK), .D(MSB));
  REG_MQ_8Bit reg_mq_8bit_1 (.DATA(Reg_MQ), .STORE_MQ(STORE), .CLOCK(CLOCK), .D(LSB));
  Multiplexer #(.Bits(8)) multiplexer_3 (.sel(LSB[0]), .in_0(MSB), .in_1(S), .out(AC_NEXT));
  // Shift_Right_16bits shift_right_16bits_1: pin names not known; wires that end beside it: {AC_NEXT, LSB}, {DATA_AC, DATA_MQ}

  // Other names for the same wires on the sheet: AC[7:0] = MSB; MQ[7:0] = LSB; MQ0 = LSB[0]; MQ1 = LSB[1];
  //   MQ2 = LSB[2]; MQ3 = LSB[3]; MQ4 = LSB[4]; MQ5 = LSB[5]; MQ6 = LSB[6]; MQ7 = LSB[7]

  // Notes on the sheet:
  //   Multiplicador Sequencial
  //   Uma multilpicação nada mais é que uma soma em cadeia
  //   O resultado de uma mult 8bit é de 16bit.
endmodule
