// Digital circuit ring_counter.dig as structural Verilog
module ring_counter (
  input  CLK,
  output T1,
  output T2,
  output T3,
  output T4,
  output T5,
  output T6
);

  wire jk_ff_1_q, jk_ff_2_nq, jk_ff_3_nq, jk_ff_4_nq, jk_ff_5_nq, jk_ff_6_nq;

  JK_FF jk_ff_1 (.J(T6), .C(CLK), .K(jk_ff_6_nq), .Q(jk_ff_1_q), .nQ(T1));
  JK_FF #(.Default(4)) jk_ff_2 (.J(T1), .C(CLK), .K(jk_ff_1_q), .Q(T2), .nQ(jk_ff_2_nq));
  JK_FF jk_ff_3 (.J(T2), .C(CLK), .K(jk_ff_2_nq), .Q(T3), .nQ(jk_ff_3_nq));
  JK_FF jk_ff_4 (.J(T3), .C(CLK), .K(jk_ff_3_nq), .Q(T4), .nQ(jk_ff_4_nq));
  JK_FF jk_ff_5 (.J(T4), .C(CLK), .K(jk_ff_4_nq), .Q(T5), .nQ(jk_ff_5_nq));
  JK_FF jk_ff_6 (.J(T5), .C(CLK), .K(jk_ff_5_nq), .Q(T6), .nQ(jk_ff_6_nq));

  // Notes on the sheet:
  //   Ring Counter
endmodule
