// Digital circuit somador+subtrator_8bits.dig as structural Verilog
module somador_subtrator_8bits (
  input  [7:0] AC,
  input  [7:0] N,
  input  SUB,
  output COUT,
  output [7:0] S
);

  wire B0, B1, B2, B3, B4, B5, B6, B7, somador_1bit_1_cout, somador_1bit_2_cout, somador_1bit_3_cout,
       somador_1bit_4_cout, somador_1bit_5_cout, somador_1bit_6_cout, somador_1bit_7_cout;

  assign {B7, B6, B5, B4, B3, B2, B1, B0} = N ^ {8{SUB}};  // XOr xor_1, 8 bits wide
  somador_1bit somador_1bit_1 (.A(AC[0]), .B(B0), .CIN(SUB), .S(S[0]), .COUT(somador_1bit_1_cout));
  somador_1bit somador_1bit_2 (.A(AC[1]), .B(B1), .CIN(somador_1bit_1_cout), .S(S[1]), .COUT(somador_1bit_2_cout));
  somador_1bit somador_1bit_3 (.A(AC[2]), .B(B2), .CIN(somador_1bit_2_cout), .S(S[2]), .COUT(somador_1bit_3_cout));
  somador_1bit somador_1bit_4 (.A(AC[3]), .B(B3), .CIN(somador_1bit_3_cout), .S(S[3]), .COUT(somador_1bit_4_cout));
  somador_1bit somador_1bit_5 (.A(AC[4]), .B(B4), .CIN(somador_1bit_4_cout), .S(S[4]), .COUT(somador_1bit_5_cout));
  somador_1bit somador_1bit_6 (.A(AC[5]), .B(B5), .CIN(somador_1bit_5_cout), .S(S[5]), .COUT(somador_1bit_6_cout));
  somador_1bit somador_1bit_7 (.A(AC[6]), .B(B6), .CIN(somador_1bit_6_cout), .S(S[6]), .COUT(somador_1bit_7_cout));
  somador_1bit somador_1bit_8 (.A(AC[7]), .B(B7), .CIN(somador_1bit_7_cout), .S(S[7]), .COUT(COUT));
  Seven_Seg_Hex seven_seg_hex_1 (.d(S[7:4]), .dp(1'b0));
  Seven_Seg_Hex seven_seg_hex_2 (.d(S[3:0]), .dp(1'b0));

  // Other names for the same wires on the sheet: A0 = AC[0]; A1 = AC[1]; A2 = AC[2]; A3 = AC[3]; A4 = AC[4];
  //   A5 = AC[5]; A6 = AC[6]; A7 = AC[7]

  // Notes on the sheet:
  //   SUB funciona como CIN:
  //   Soma --> CIN/SUB = 0
  //   Sub --> CIN/SUB = 1
  //   Somador e subtrator de 8 bits
  //   B | SUB | BN
  //   0  |    0   |   0
  //   0  |    1   |   1
  //   1  |    0   |   1 
  //   1  |    1   |   0
endmodule
