// Digital circuit somador_1bit.dig as structural Verilog
module somador_1bit (
  input  A,
  input  B,
  input  CIN,
  output S,
  output COUT
);

  wire and_1_out, and_2_out, xor_1_out;

  xor xor_1 (xor_1_out, A, B);
  xor xor_2 (S, xor_1_out, CIN);
  and and_1 (and_1_out, CIN, xor_1_out);
  and and_2 (and_2_out, B, A);
  or or_1 (COUT, and_1_out, and_2_out);

  // Notes on the sheet:
  //   Somador Completo
endmodule
