// Digital circuit somador_8bits.dig as structural Verilog
module somador_8bits (
  input  [7:0] A,
  input  [7:0] B,
  input  CIN,
  output COUT,
  output [7:0] S
);

  wire somador_1bit_1_cout, somador_1bit_2_cout, somador_1bit_3_cout, somador_1bit_4_cout,
       somador_1bit_5_cout, somador_1bit_6_cout, somador_1bit_7_cout;

  somador_1bit somador_1bit_1 (.A(A[0]), .B(B[0]), .CIN(CIN), .S(S[0]), .COUT(somador_1bit_1_cout));
  somador_1bit somador_1bit_2 (.A(A[1]), .B(B[1]), .CIN(somador_1bit_1_cout), .S(S[1]), .COUT(somador_1bit_2_cout));
  somador_1bit somador_1bit_3 (.A(A[2]), .B(B[2]), .CIN(somador_1bit_2_cout), .S(S[2]), .COUT(somador_1bit_3_cout));
  somador_1bit somador_1bit_4 (.A(A[3]), .B(B[3]), .CIN(somador_1bit_3_cout), .S(S[3]), .COUT(somador_1bit_4_cout));
  somador_1bit somador_1bit_5 (.A(A[4]), .B(B[4]), .CIN(somador_1bit_4_cout), .S(S[4]), .COUT(somador_1bit_5_cout));
  somador_1bit somador_1bit_6 (.A(A[5]), .B(B[5]), .CIN(somador_1bit_5_cout), .S(S[5]), .COUT(somador_1bit_6_cout));
  somador_1bit somador_1bit_7 (.A(A[6]), .B(B[6]), .CIN(somador_1bit_6_cout), .S(S[6]), .COUT(somador_1bit_7_cout));
  somador_1bit somador_1bit_8 (.A(A[7]), .B(B[7]), .CIN(somador_1bit_7_cout), .S(S[7]), .COUT(COUT));
  Seven_Seg_Hex seven_seg_hex_1 (.d(S[7:4]), .dp(1'b0));
  Seven_Seg_Hex seven_seg_hex_2 (.d(S[3:0]), .dp(1'b0));

  // Notes on the sheet:
  //   Somador de 8 bits
endmodule
