// Digital circuit subtrator_8bits.dig as structural Verilog
module subtrator_8bits (
  input  [7:0] A,
  input  [7:0] B,
  input  CIN,
  output COUT,
  output [7:0] S
);

  wire [7:0] not_1_out;

  assign not_1_out = ~B;  // Not not_1, 8 bits wide
  somador_8bits somador_8bits_1 (.A(A), .B(not_1_out), .CIN(CIN), .COUT(COUT), .S(S));

  // Notes on the sheet:
  //   Subtrator de 8 bits
endmodule
